// Logisim project Lab-1.circ as structural Verilog: 1 circuit, main circuit main
module main (
  input  in_1,
  input  in_2,
  input  in_3,
  input  in_4,
  input  in_5,
  input  in_6,
  input  in_7,
  input  in_8,
  input  in_9,
  input  in_10,
  input  in_11,
  input  in_12,
  input  in_13,
  input  in_14,
  input  in_15,
  input  in_16,
  input  in_17,
  input  in_18,
  input  in_19,
  input  in_20,
  input  in_21,
  input  in_22,
  input  in_23,
  output out_24,
  output out_25,
  output out_26,
  output out_27,
  output out_28,
  output out_29,
  output out_30,
  output out_31,
  output out_32
);

  wire and_2_out, and_4_out, and_5_out, and_6_out, not_2_out, not_3_out, or_2_out, or_4_out;

  and and_1 (out_24, in_1, in_2);
  or or_1 (out_25, in_3, in_4);
  not not_1 (out_26, in_6);
  nand nand_1 (out_27, in_8, in_9);
  nor nor_1 (out_29, in_11, in_13);
  xor xor_1 (out_30, in_14, in_16);
  and and_2 (and_2_out, in_18, in_19);
  or or_2 (or_2_out, in_21, in_22);
  and and_3 (out_31, and_2_out, in_20);
  or or_3 (out_32, or_2_out, in_23);
  not not_2 (not_2_out, in_5);
  not not_3 (not_3_out, in_12);
  and and_4 (and_4_out, not_2_out, in_7);
  and and_5 (and_5_out, in_10, not_3_out);
  and and_6 (and_6_out, in_15, in_17);
  or or_4 (or_4_out, and_4_out, and_5_out);
  or or_5 (out_28, or_4_out, and_6_out);

  // Notes on the sheet:
  //   CSE 231.9
  //   Shakil Ahmed
  //   ID: 2221453042
  //   Faculty Initial: 2221453042
endmodule
